// Logisim project CPU_LoongArch.circ as structural Verilog
module ALU (
  input  [3:0] alu_op,
  input  [31:0] src1,
  input  [31:0] src2,
  output [31:0] alu_res
);

  wire adder_1_cout, and_1_out, and_2_out, multiplexer_2_out, multiplexer_3_out, not_2_out, slt_out,
       slt_sltu_out, xor_1_out;
  wire [1:1] alu_res_sel;
  wire [31:0] adder_1_out, bit_extender_1_out, multiplexer_1_out, multiplexer_4_out, not_1_out,
       shifter_1_out, shifter_3_out;

  Multiplexer #(.width(32)) multiplexer_1 (.in0(src2), .in1(not_1_out), .out(multiplexer_1_out), .sel(alu_op[0]));
  assign not_1_out = ~src2;  // NOT_Gate not_1, 32 bits wide
  xor xor_1 (xor_1_out, src1[31], src2[31]);
  or shift_ifornot (alu_res_sel[1], alu_op[2], alu_op[3]);
  and and_1 (and_1_out, src1[31], xor_1_out);
  not not_2 (not_2_out, xor_1_out);
  Multiplexer multiplexer_2 (.in0(1'b0), .in1(1'b1), .out(multiplexer_2_out), .sel(alu_op[0]));
  Adder #(.width(32)) adder_1 (
    .a(src1), .b(multiplexer_1_out), .out(adder_1_out), .cin(multiplexer_2_out), .cout(adder_1_cout));
  Multiplexer multiplexer_3 (.in0(1'b1), .in1(1'b0), .out(multiplexer_3_out), .sel(adder_1_cout));
  Shifter #(.width(32)) shifter_1 (.in(src1), .\dist (src2[4:0]), .out(shifter_1_out));
  Shifter #(.shift("lr"), .width(32)) shifter_2 (.in(src1), .\dist (src2[4:0]), .out(shifter_1_out));
  Shifter #(.shift("ar"), .width(32)) shifter_3 (.in(src1), .\dist (src2[4:0]), .out(shifter_3_out));
  and and_2 (and_2_out, adder_1_out[31], not_2_out);
  or slt (slt_out, and_2_out, and_1_out);
  Multiplexer #(.select(2), .width(32)) multiplexer_4 (
    .in0(src2), .in1(shifter_1_out), .in2(shifter_1_out), .in3(shifter_3_out), .out(multiplexer_4_out),
    .sel(alu_op[3:2]));
  or slt_sltu (slt_sltu_out, slt_out, multiplexer_3_out);
  assign bit_extender_1_out = {{31{1'b0}}, slt_sltu_out};  // Bit_Extender bit_extender_1
  Multiplexer #(.select(2), .width(32)) multiplexer_5 (
    .in0(adder_1_out), .in1(bit_extender_1_out), .in2(multiplexer_4_out), .out(alu_res),
    .sel({alu_res_sel[1], alu_op[1]}));  // open: in3

  // Other names for the same wires on the sheet: shift_sel[1:0] = alu_op[3:2]; alu_res_sel[0] = alu_op[1]

  // Notes on the sheet:
  //   0位:加法还是减法  为1指令:sub.w,slt,sltu
  //   slt逻辑
  //   1位:是不是slt(u)，结果选择  为1指令:slt,sltu
  //   2-3位:移位操作，00不是移位  01逻辑左  10逻辑右  11算术右
  //   if (A[31] != B[31])  A < B = A[31]
  //   else  A < B = (A - B)
  //   sel_notsrc2
  //   为1的指令:sub.w,slt,sltu
  //   为1的指令:sub.w,slt,sltu
  //   sel_cin
  //   sel_cout
  //   sltu，相减的cout为0的时候置位
  //   1:slt,sltu
  //   alu_op来选择
  //   2:slli.w,srli.w,srai.w
endmodule
